// Digital circuit 4bit_ALU.dlogic.dig as structural Verilog
module _4bit_ALU_dlogic (
  input  [2:0] Ci_2,
  input  [3:0] A,
  input  [3:0] B,
  input  [3:0] _0,
  input  [3:0] _0_2,
  input  _0_6,
  input  _0_7,
  input  _0_8,
  output [3:0] Output,
  output Zero_Flag,
  output _0_3,
  output _0_4,
  output _0_5,
  output SLT_flag
);

  wire [2:0] _4bit_subtractor_1_result;
  wire [3:0] and_1_out, or_1_out, xor_1_out;

  _4bit_subtractor _4bit_subtractor_1 (
    .B(B), .A(A), .K(Ci_2[0]), .Result({SLT_flag, _4bit_subtractor_1_result}), .Cout(_0_5));
  assign and_1_out = A & B;  // And and_1, 4 bits wide
  assign or_1_out = A | B;  // Or or_1, 4 bits wide
  assign xor_1_out = A ^ B;  // XOr xor_1, 4 bits wide
  Multiplexer #(.Selector_Bits(3), .Bits(4)) multiplexer_1 (
    .sel(Ci_2), .in_0({SLT_flag, _4bit_subtractor_1_result}), .in_1({SLT_flag, _4bit_subtractor_1_result}),
    .in_2(and_1_out), .in_3(or_1_out), .in_4(xor_1_out), .in_5({_0_6, _0_8, _0_7, SLT_flag}), .in_6(_0),
    .in_7(_0_2), .out(Output));
  nor nor_1 (Zero_Flag, _4bit_subtractor_1_result[0], _4bit_subtractor_1_result[1], _4bit_subtractor_1_result[2], SLT_flag);

  assign _0_3 = Ci_2[1];
  assign _0_4 = Ci_2[2];

  // Notes on the sheet:
  //   Output: Could be literally 4 indivisual bits tho
endmodule
