// Digital circuit 4bit_subtractor.dig as structural Verilog
module _4bit_subtractor (
  input  [3:0] B,
  input  [3:0] A,
  input  K,
  output [3:0] Result,
  output Cout
);

  wire _1bit_full_adder_2_cout, _1bit_full_adder_3_cout, _1bit_full_adder_4_cout, xor_1_out, xor_2_out,
       xor_3_out, xor_4_out;

  xor xor_1 (xor_1_out, K, B[3]);
  _1bit_full_adder _1bit_full_adder_1 (
    .A(A[3]), .B(xor_1_out), .Cin(_1bit_full_adder_2_cout), .Sum(Result[3]), .Cout(Cout));
  xor xor_2 (xor_2_out, K, B[2]);
  _1bit_full_adder _1bit_full_adder_2 (
    .A(A[2]), .B(xor_2_out), .Cin(_1bit_full_adder_3_cout), .Sum(Result[2]), .Cout(_1bit_full_adder_2_cout));
  xor xor_3 (xor_3_out, K, B[1]);
  _1bit_full_adder _1bit_full_adder_3 (
    .A(A[1]), .B(xor_3_out), .Cin(_1bit_full_adder_4_cout), .Sum(Result[1]), .Cout(_1bit_full_adder_3_cout));
  xor xor_4 (xor_4_out, K, B[0]);
  _1bit_full_adder _1bit_full_adder_4 (
    .A(A[0]), .B(xor_4_out), .Cin(K), .Sum(Result[0]), .Cout(_1bit_full_adder_4_cout));
endmodule
